// Logisim project TIC_TAC_TOE.circ as structural Verilog: 1 circuit, main circuit main
module main (
  output W,
  output A11,
  output A12,
  output A13,
  output A21,
  output A22,
  output A23,
  output A31,
  output A32,
  output A33,
  output B11,
  output B12,
  output B13,
  output B21,
  output B22,
  output B23,
  output B31,
  output B32,
  output B33,
  output W_2
);

  wire and_1_out, and_2_out, and_3_out, and_4_out, and_5_out, and_6_out, and_7_out, and_8_out, and_9_out,
       and_10_out, and_11_out, and_12_out, and_13_out, and_14_out, and_15_out, and_16_out, and_17_out,
       and_18_out, and_19_out, and_20_out, and_21_out, and_22_out, and_23_out, and_24_out, and_25_out,
       and_26_out, and_27_out, and_28_out, and_29_out, and_30_out, and_31_out, and_32_out, and_33_out,
       and_34_out, button_1_out, button_2_out, button_3_out, button_4_out, button_5_out, button_6_out,
       button_7_out, button_8_out, button_9_out, button_10_out, button_11_out, button_12_out, button_13_out,
       button_14_out, button_15_out, button_16_out, button_17_out, button_18_out, d_ff_19_q, d_ff_20_q,
       not_1_out, not_2_out, not_3_out, not_4_out, not_5_out, not_6_out, not_7_out, not_8_out, not_9_out,
       not_10_out, not_11_out, not_12_out, not_13_out, not_14_out, not_15_out, not_16_out, not_17_out,
       not_18_out, or_3_out;

  Button button_1 (.out(button_1_out));
  Button button_2 (.out(button_2_out));
  Button button_3 (.out(button_3_out));
  Button button_4 (.out(button_4_out));
  Button button_5 (.out(button_5_out));
  Button button_6 (.out(button_6_out));
  Button button_7 (.out(button_7_out));
  Button button_8 (.out(button_8_out));
  Button button_9 (.out(button_9_out));
  Button button_10 (.out(button_10_out));
  Button button_11 (.out(button_11_out));
  Button button_12 (.out(button_12_out));
  Button button_13 (.out(button_13_out));
  Button button_14 (.out(button_14_out));
  Button button_15 (.out(button_15_out));
  Button button_16 (.out(button_16_out));
  Button button_17 (.out(button_17_out));
  Button button_18 (.out(button_18_out));
  and and_1 (and_1_out, button_8_out, not_1_out);
  not not_1 (not_1_out, B11);
  and and_2 (and_2_out, button_1_out, not_2_out);
  not not_2 (not_2_out, A11);
  D_Flip_Flop d_ff_1 (.clk(and_1_out), .D(and_1_out), .Q(A11), .reset(or_3_out));  // open: Qn, preset, en
  D_Flip_Flop d_ff_2 (.clk(and_2_out), .D(and_2_out), .Q(B11), .reset(or_3_out));  // open: Qn, preset, en
  and and_3 (and_3_out, button_10_out, not_3_out);
  not not_3 (not_3_out, B21);
  and and_4 (and_4_out, button_4_out, not_4_out);
  not not_4 (not_4_out, A21);
  and and_5 (and_5_out, button_11_out, not_5_out);
  not not_5 (not_5_out, B31);
  and and_6 (and_6_out, button_5_out, not_6_out);
  not not_6 (not_6_out, A31);
  D_Flip_Flop d_ff_3 (.clk(and_3_out), .D(and_3_out), .Q(A21), .reset(or_3_out));  // open: Qn, preset, en
  D_Flip_Flop d_ff_4 (.clk(and_4_out), .D(and_4_out), .Q(B21), .reset(or_3_out));  // open: Qn, preset, en
  D_Flip_Flop d_ff_5 (.clk(and_5_out), .D(and_5_out), .Q(A31), .reset(or_3_out));  // open: Qn, preset, en
  D_Flip_Flop d_ff_6 (.clk(and_6_out), .D(and_6_out), .Q(B31), .reset(or_3_out));  // open: Qn, preset, en
  and and_7 (and_7_out, button_7_out, not_7_out);
  not not_7 (not_7_out, B12);
  and and_8 (and_8_out, button_2_out, not_8_out);
  not not_8 (not_8_out, A12);
  D_Flip_Flop d_ff_7 (.clk(and_7_out), .D(and_7_out), .Q(A12), .reset(or_3_out));  // open: Qn, preset, en
  D_Flip_Flop d_ff_8 (.clk(and_8_out), .D(and_8_out), .Q(B12), .reset(or_3_out));  // open: Qn, preset, en
  not not_9 (not_9_out, B22);
  not not_10 (not_10_out, A22);
  not not_11 (not_11_out, B32);
  not not_12 (not_12_out, A32);
  not not_13 (not_13_out, B13);
  not not_14 (not_14_out, A13);
  D_Flip_Flop d_ff_9 (.clk(and_9_out), .D(and_9_out), .Q(A22), .reset(or_3_out));  // open: Qn, preset, en
  and and_9 (and_9_out, button_9_out, not_9_out);
  D_Flip_Flop d_ff_10 (.clk(and_10_out), .D(and_10_out), .Q(B22), .reset(or_3_out));  // open: Qn, preset, en
  and and_10 (and_10_out, button_3_out, not_10_out);
  D_Flip_Flop d_ff_11 (.clk(and_11_out), .D(and_11_out), .Q(A32), .reset(or_3_out));  // open: Qn, preset, en
  and and_11 (and_11_out, button_12_out, not_11_out);
  D_Flip_Flop d_ff_12 (.clk(and_12_out), .D(and_12_out), .Q(B32), .reset(or_3_out));  // open: Qn, preset, en
  and and_12 (and_12_out, button_6_out, not_12_out);
  LED led_1 (.in(B11));
  LED led_2 (.in(A11));
  LED led_3 (.in(A21));
  LED led_4 (.in(B21));
  LED led_5 (.in(A31));
  LED led_6 (.in(B31));
  D_Flip_Flop d_ff_13 (.clk(and_13_out), .D(and_13_out), .Q(A13), .reset(or_3_out));  // open: Qn, preset, en
  and and_13 (and_13_out, button_16_out, not_13_out);
  D_Flip_Flop d_ff_14 (.clk(and_14_out), .D(and_14_out), .Q(B13), .reset(or_3_out));  // open: Qn, preset, en
  and and_14 (and_14_out, button_13_out, not_14_out);
  not not_15 (not_15_out, B23);
  not not_16 (not_16_out, A23);
  not not_17 (not_17_out, B33);
  not not_18 (not_18_out, A33);
  LED led_7 (.in(B12));
  LED led_8 (.in(A12));
  LED led_9 (.in(B22));
  LED led_10 (.in(A22));
  LED led_11 (.in(B32));
  LED led_12 (.in(A32));
  and and_15 (and_15_out, button_17_out, not_15_out);
  and and_16 (and_16_out, button_14_out, not_16_out);
  and and_17 (and_17_out, button_18_out, not_17_out);
  and and_18 (and_18_out, button_15_out, not_18_out);
  LED led_13 (.in(B13));
  LED led_14 (.in(A13));
  LED led_15 (.in(A23));
  LED led_16 (.in(A33));
  D_Flip_Flop d_ff_15 (.clk(and_15_out), .D(and_15_out), .Q(A23), .reset(or_3_out));  // open: Qn, preset, en
  D_Flip_Flop d_ff_16 (.clk(and_16_out), .D(and_16_out), .Q(B23), .reset(or_3_out));  // open: Qn, preset, en
  D_Flip_Flop d_ff_17 (.clk(and_17_out), .D(and_17_out), .Q(A33), .reset(or_3_out));  // open: Qn, preset, en
  D_Flip_Flop d_ff_18 (.clk(and_18_out), .D(and_18_out), .Q(B33), .reset(or_3_out));  // open: Qn, preset, en
  LED led_17 (.in(B23));
  LED led_18 (.in(B33));
  and and_19 (and_19_out, A11, A12, A13);
  and and_20 (and_20_out, A21, A22, A23);
  and and_21 (and_21_out, A31, A32, A33);
  and and_22 (and_22_out, A11, A22, A33);
  and and_23 (and_23_out, A11, A21, A31);
  and and_24 (and_24_out, A12, A22, A32);
  and and_25 (and_25_out, A13, A23, A33);
  and and_26 (and_26_out, A13, A22, A31);
  and and_27 (and_27_out, B11, B12, B13);
  and and_28 (and_28_out, B23, B13, B33);
  and and_29 (and_29_out, B31, B32, B33);
  and and_30 (and_30_out, B11, B22, B33);
  and and_31 (and_31_out, B11, B21, B31);
  and and_32 (and_32_out, B12, B22, B32);
  and and_33 (and_33_out, B22, B21, B23);
  and and_34 (and_34_out, B13, B22, B31);
  or or_1 (W, and_19_out, and_20_out, and_21_out, and_22_out, and_23_out, and_24_out, and_25_out, and_26_out);
  or or_2 (W_2, and_27_out, and_28_out, and_29_out, and_30_out, and_31_out, and_32_out, and_33_out, and_34_out);
  D_Flip_Flop d_ff_19 (.clk(W), .D(W), .Q(d_ff_19_q));  // open: Qn, preset, en, reset
  LED led_19 (.in(d_ff_19_q));
  or or_3 (or_3_out, W, W_2);
  D_Flip_Flop d_ff_20 (.clk(W_2), .D(W_2), .Q(d_ff_20_q));  // open: Qn, preset, en, reset
  LED led_20 (.in(d_ff_20_q));

  // Notes on the sheet:
  //   PLAYER
  //   1
  //   PLAYER
  //   2
  //   Result instruction:
  //   Enjoy the Game!
  //   For resetting the board press: Ctrl + R
  //   2. If none of the lights are glowing then the game is draw.
  //   1. If either of the light glows then the light which glows is the winner.
  //   WINNER
  //   TIC TAC TOE
  //   GRID
  //   Green
  //   BLue
  //   4. Belwo circuit for blue player.
  //   3. Above  circuit is for green player.
  //   1. Eight such winning combinations are possible for each player to win
  //   2. Below given circuit gives the output for win (w) if any of the player won the game
  //   5. D-flipflops are utilized to remeber the respective input of the player 
  //   6. Also if one input is being registered by the player then other player cannot make the same input
endmodule
